# Fritzing sketch 2-Boiler-controlled-by-Arduino (saved by Fritzing 0.9.2b)
breadboards: 1

parts:
  Part1 = Arduino Uno (Rev3)
  U2 = RELAY [package=relay-g5q]
  Q1 = NPN-Transistor [package="SOT-23 [SMD]"]
  R1 = Resistor [tolerance=±5% resistance=2.2k package=THT]
  D1 = Rectifier Diode [part_number=1N4001 package="300 mil [THT]"]
  J1 = Screw terminal - 2 pins [package=THT]
  U3 = RELAY [package=relay-g5q]
  R2 = Resistor [tolerance=±5% resistance=2.2k package=THT]
  D2 = Rectifier Diode [part_number=1N4001 package="300 mil [THT]"]
  J2 = Screw terminal - 2 pins [package=THT]
  Q2 = NPN-Transistor [package="SOT-23 [SMD]"]
  J3 = screw terminal, 3 pins

nets:
  N1: Part1.A0, J3.pin2
  N2: Part1.A1, J3.pin1
  N3: Part1.D2, R1.Pin_0
  N4: Part1.D3_PWM, R2.Pin_0
  N5: Part1.5V, U2.NC, D1.cathode, U3.NC, D2.cathode
  N6: Part1.GND, Q1.2, Q2.2, J3.pin3
  N7: U2.MAIN, J1.pin2
  N8: U2.NO, J1.pin1
  N9: U2.COIL1, Q1.1, D1.anode
  N10: Q1.0, R1.Pin_1
  N11: U3.MAIN, J2.pin2
  N12: U3.NO, J2.pin1
  N13: U3.COIL1, D2.anode, Q2.1
  N14: R2.Pin_1, Q2.0
