# Fritzing sketch 4-Indicators-with-Arduino (saved by Fritzing 0.9.4)
breadboards: 1

parts:
  Part1 = Arduino Uno (Rev3)
  U2 = RELAY [package=relay-g5q]
  Q1 = NPN-Transistor [package="SOT-23 [SMD]"]
  R1 = Resistor [tolerance=±5% resistance=2.2k package=THT]
  D1 = Rectifier Diode [part_number=1N4001 package="300 mil [THT]"]
  J1 = Screw terminal - 2 pins [package=THT]
  U3 = RELAY [package=relay-g5q]
  R2 = Resistor [tolerance=±5% resistance=2.2k package=THT]
  D2 = Rectifier Diode [part_number=1N4001 package="300 mil [THT]"]
  J2 = Screw terminal - 2 pins [package=THT]
  Q2 = NPN-Transistor [package="SOT-23 [SMD]"]
  J3 = screw terminal, 3 pins
  R3 = Resistor [tolerance=±5% resistance=4.7k package=THT]
  J4 = screw terminal, 2 pins
  J5 = screw terminal, 2 pins
  J6 = screw terminal, 2 pins
  R4 = Resistor [tolerance=±5% resistance=330 package=THT]
  LED1 = LED - 5mm [color="Red (633nm)" package="5 mm [THT]"]
  R5 = Resistor [tolerance=±5% resistance=330 package=THT]
  LED2 = LED - 5mm [color="Green (555nm)" package="5 mm [THT]"]

nets:
  N1: Part1.A0, J3.pin2
  N2: Part1.A1, J3.pin1
  N3: Part1.A2, R3.Pin_1, J4.pin1
  N4: Part1.D2, R1.Pin_0
  N5: Part1.D3_PWM, R2.Pin_0, R4.Pin_1
  N6: Part1.D4, R5.Pin_1
  N7: Part1.5V, U2.NC, D1.cathode, U3.NC, D2.cathode, J4.pin2
  N8: Part1.GND, Q1.2, Q2.2, J3.pin3, R3.Pin_0, J5.pin1, J6.pin1, LED1.cathode, LED2.cathode
  N9: U2.MAIN, J1.pin2
  N10: U2.NO, J1.pin1
  N11: U2.COIL1, Q1.1, D1.anode
  N12: Q1.0, R1.Pin_1
  N13: U3.MAIN, J2.pin2
  N14: U3.NO, J2.pin1
  N15: U3.COIL1, D2.anode, Q2.1
  N16: R2.Pin_1, Q2.0
  N17: J5.pin2, R5.Pin_0, LED2.anode
  N18: R4.Pin_0, LED1.anode
