# Fritzing sketch 5-Final-NodeMCU (saved by Fritzing 0.9.4)
breadboards: 1

parts:
  U2 = RELAY [package=relay-g5q]
  Q1 = NPN-Transistor [package="SOT-23 [SMD]"]
  R1 = Resistor [tolerance=±5% resistance=2.2k package=THT]
  D1 = Rectifier Diode [part_number=1N4001 package="300 mil [THT]"]
  J1 = Screw terminal - 2 pins [package=THT]
  U3 = RELAY [package=relay-g5q]
  R2 = Resistor [tolerance=±5% resistance=2.2k package=THT]
  D2 = Rectifier Diode [part_number=1N4001 package="300 mil [THT]"]
  J2 = Screw terminal - 2 pins [package=THT]
  Q2 = NPN-Transistor [package="SOT-23 [SMD]"]
  J3 = screw terminal, 3 pins
  R3 = Resistor [tolerance=±5% resistance=4.7k package=THT]
  J4 = screw terminal, 2 pins
  J5 = screw terminal, 2 pins
  J6 = screw terminal, 2 pins
  R4 = Resistor [tolerance=±5% resistance=330 package=THT]
  LED1 = LED - 5mm [color="Red (633nm)" package="5 mm [THT]"]
  R5 = Resistor [tolerance=±5% resistance=330 package=THT]
  LED2 = LED - 5mm [color="Green (555nm)" package="5 mm [THT]"]
  U4 = NodeMCU V3.0
  HLK-PM1 = HLK-PM01

nets:
  N1: U2.MAIN, J1.pin2
  N2: U2.NO, J1.pin1
  N3: U2.NC, D1.cathode, U3.NC, D2.cathode, U4.Vin, HLK-PM1.+Vo
  N4: U2.COIL1, Q1.1, D1.anode
  N5: Q1.2, Q2.2, J3.pin3, R3.Pin_0, J5.pin1, J6.pin1, LED1.cathode, LED2.cathode, U4.GND
  N6: Q1.0, R1.Pin_1
  N7: R1.Pin_0, U4.D1
  N8: U3.MAIN, J2.pin2
  N9: U3.NO, J2.pin1
  N10: U3.COIL1, D2.anode, Q2.1
  N11: R2.Pin_0, R4.Pin_1, U4.D2
  N12: R2.Pin_1, Q2.0
  N13: J3.pin1, U4.D6
  N14: J3.pin2, U4.D5
  N15: R3.Pin_1, J4.pin1, U4.A0
  N16: J4.pin2, U4.3V3
  N17: J5.pin2, R5.Pin_0, LED2.anode
  N18: R4.Pin_0, LED1.anode
  N19: R5.Pin_1, U4.D7
  N20: U4.RSV, HLK-PM1.-Vo

custom parts:
  NodeMCU V3.0: NodeMcu V3 Lua WIFI Development Board
