# Fritzing sketch Relay-controlled-by-NodeMCU (saved by Fritzing 0.9.4)
breadboards: 1

parts:
  U4 = NodeMCU V3.0
  J1 = Screw terminal - 2 pins [package=THT]
  Q1 = NPN-Transistor [package="SOT-23 [SMD]"]
  U2 = RELAY [package=relay-g5q]
  D1 = Rectifier Diode [part_number=1N4001 package="300 mil [THT]"]
  R1 = Resistor [tolerance=±5% resistance=2.2k package=THT]

nets:
  N1: U4.D1, R1.Pin_0
  N2: U4.GND, Q1.2
  N3: U4.Vin, U2.NC, D1.cathode
  N4: J1.pin1, U2.NO
  N5: J1.pin2, U2.MAIN
  N6: Q1.0, R1.Pin_1
  N7: Q1.1, U2.COIL1, D1.anode

custom parts:
  NodeMCU V3.0: NodeMcu V3 Lua WIFI Development Board
