# Fritzing sketch Scheme (saved by Fritzing 0.9.2b)
breadboards: 1

parts:
  Part1 = Arduino Uno (Rev3)
  U2 = RELAY [package=relay-g5q]
  Q1 = NPN-Transistor [package="SOT-23 [SMD]"]
  R1 = Resistor [tolerance=±5% resistance=2.2k package=THT]
  D1 = Rectifier Diode [part_number=1N4001 package="300 mil [THT]"]
  J1 = Screw terminal - 2 pins [package=THT]

nets:
  N1: Part1.D2, R1.Pin_0
  N2: Part1.5V, U2.NC, D1.cathode
  N3: Part1.GND, Q1.2
  N4: U2.COIL2, J1.pin2
  N5: U2.MAIN, J1.pin1
  N6: U2.COIL1, Q1.1, D1.anode
  N7: Q1.0, R1.Pin_1
